# Fritzing sketch SciOxProject2025 (saved by Fritzing 1.0.3b)
circuit board: 8.46667cm x 5.64444cm
breadboards: 2

parts:
  M1 = DOIT Esp32 DevKit v1 (30 pins long, 11 pins width) [part_number=ESP32S-PIN30]
  M2 = pcf8574 io expansion board [package=THT]
  A1 = ENS160 AHT21
  S1 = Pushbutton [package="[THT]"]

nets:
  N1: M1.3V3, A1.Pin_2, S1.Pin_3, S1.Pin_4
  GND: M1.GND, M2.GND, A1.Pin_3
  N2: M1.TX2, S1.Pin_1, S1.Pin_2
  N3: M1.D18, M2.SCL
  N4: M1.D19, M2.SDA
  N5: M1.D25, A1.Pin_4
  N6: M1.D26, A1.Pin_5

custom parts:
  DOIT Esp32 DevKit v1 (30 pins long, 11 pins width): The DOIT Esp32 DevKit v1 is one of the development board created by DOIT to evaluate the ESP-WROOM-32 module. It is based on the ESP32 microcontroller that boasts Wifi, Bluetooth, Ethernet and Low Power support all in a single chip. (vanepp) made breadboard work, adjusted pin numbering and labels and reduced size of schematic and cleaned up pcb. This chip is 30pins long (2 x15) and 11 pins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
  pcf8574 io expansion board: pcf8574 io expansion board.
  ENS160 AHT21: The CO2 Gas- Air- Sensor is based on ENS160 in combination with an AHT21 Temperature Humidity Sensor.
